# Fritzing sketch XIAO-scope-Sketch (saved by Fritzing 0.9.4)
breadboards: 1

parts:
  Mod1 = seeeduino-xiao
  C1 = Ceramic Capacitor [capacitance=100nF package="100 mil [THT, multilayer]"]
  R1 = Resistor [tolerance=±5% resistance=1k package=THT]
  R2 = Resistor [tolerance=±5% resistance=220 package=THT]
  R3 = Resistor [tolerance=±5% resistance=220 package=THT]

nets:
  N1: Mod1.D0, Mod1.D1, R1.Pin_1
  N2: Mod1.D2, C1.1, R1.Pin_0
  N3: Mod1.3V3, R3.Pin_1
  N4: Mod1.GND, C1.0, R2.Pin_1
  N5: R2.Pin_0, R3.Pin_0

custom parts:
  seeeduino-xiao: Seeeduino XIAO processor board.
