# Fritzing sketch XIAO-scope-awg-pwm (saved by Fritzing 0.9.4)
breadboards: 1

parts:
  XIAO = seeeduino-xiao
  C1 = Ceramic Capacitor [capacitance=0.22µF package="100 mil [THT, multilayer]"]
  R1 = Resistor [tolerance=±5% resistance=1.5k package=THT]

nets:
  N1: XIAO.D0, XIAO.D1
  N2: XIAO.D2, C1.1, R1.Pin_0
  N3: XIAO.D10, R1.Pin_1
  N4: XIAO.GND, C1.0

custom parts:
  seeeduino-xiao: Seeeduino XIAO processor board.
