# Fritzing sketch XIAO-scope-diode-i (saved by Fritzing 0.9.4)
breadboards: 1

parts:
  XIAO = seeeduino-xiao
  R1 = Resistor [tolerance=±5% resistance=150 package=THT]
  R2 = Resistor [tolerance=±5% resistance=100 package=THT]
  R3 = Resistor [tolerance=±5% resistance=100 package=THT]
  D1 = Rectifier Diode [part_number=1N914 package="300 mil [THT]"]

nets:
  N1: XIAO.D0, XIAO.D1, R1.Pin_1
  N2: XIAO.D2, R1.Pin_0, D1.anode
  N3: XIAO.D3, R2.Pin_0, R3.Pin_0, D1.cathode
  N4: XIAO.3V3, R3.Pin_1
  N5: XIAO.GND, R2.Pin_1

custom parts:
  seeeduino-xiao: Seeeduino XIAO processor board.
