# Fritzing sketch XIAO-scope-in-divider (saved by Fritzing 0.9.4)
breadboards: 1

parts:
  XIAO = seeeduino-xiao
  R1 = Resistor [tolerance=±5% resistance=220k package=THT]
  R2 = Resistor [tolerance=±5% resistance=100k package=THT]
  R3 = Resistor [tolerance=±5% resistance=100k package=THT]
  R4 = Resistor [tolerance=±5% resistance=220k package=THT]
  R5 = Resistor [tolerance=±5% resistance=220k package=THT]
  R6 = Resistor [tolerance=±5% resistance=100k package=THT]
  R7 = Resistor [tolerance=±5% resistance=100k package=THT]
  R8 = Resistor [tolerance=±5% resistance=100k package=THT]
  R9 = Resistor [tolerance=±5% resistance=100k package=THT]

nets:
  N1: XIAO.D1, R1.Pin_0, R2.Pin_0, R3.Pin_0
  N2: XIAO.D2, R4.Pin_0, R6.Pin_0, R7.Pin_0
  N3: XIAO.D3, R5.Pin_0, R8.Pin_0, R9.Pin_0
  N4: XIAO.3V3, R3.Pin_1, R6.Pin_1, R9.Pin_1
  N5: XIAO.GND, R2.Pin_1, R7.Pin_1, R8.Pin_1

custom parts:
  seeeduino-xiao: Seeeduino XIAO processor board.
