# Fritzing sketch XIAO-scope-npn-amp (saved by Fritzing 0.9.4)
breadboards: 1

parts:
  XIAO = seeeduino-xiao
  R2 = Resistor [tolerance=±5% resistance=1k package=THT]
  R1 = Resistor [tolerance=±5% resistance=1k package=THT]
  Q1 = NPN-Transistor [package="TO92 [THT]"]

nets:
  N1: XIAO.D0, XIAO.D1, Q1.B
  N2: XIAO.D2, R2.Pin_0, Q1.E
  N3: XIAO.D3, R1.Pin_0, Q1.C
  N4: XIAO.3V3, R1.Pin_1
  N5: XIAO.GND, R2.Pin_1

custom parts:
  seeeduino-xiao: Seeeduino XIAO processor board.
