# Fritzing sketch XIAO-scope-r-c-i (saved by Fritzing 0.9.4)
breadboards: 1

parts:
  XIAO = seeeduino-xiao
  C1 = Ceramic Capacitor [capacitance=0.22µF package="100 mil [THT, multilayer]"]
  R1 = Resistor [tolerance=±5% resistance=1k package=THT]
  R2 = Resistor [tolerance=±5% resistance=100 package=THT]
  R3 = Resistor [tolerance=±5% resistance=100 package=THT]

nets:
  N1: XIAO.D0, XIAO.D1, R1.Pin_1
  N2: XIAO.D2, C1.0, R1.Pin_0
  N3: XIAO.D3, C1.1, R2.Pin_0, R3.Pin_0
  N4: XIAO.3V3, R3.Pin_1
  N5: XIAO.GND, R2.Pin_1

custom parts:
  seeeduino-xiao: Seeeduino XIAO processor board.
